# Fritzing sketch RGB Light Chaser (saved by Fritzing 0.9.0b)
breadboards: 2

parts:
  LED1 = RGB LED (com. cathode, rbg) [package="5 mm [THT]"]
  LED2 = RGB LED (com. cathode, rbg) [package="5 mm [THT]"]
  LED3 = RGB LED (com. cathode, rbg) [package="5 mm [THT]"]
  LED4 = RGB LED (com. cathode, rbg) [package="5 mm [THT]"]
  LED5 = RGB LED (com. cathode, rbg) [package="5 mm [THT]"]
  LED6 = RGB LED (com. cathode, rbg) [package="5 mm [THT]"]
  LED7 = RGB LED (com. cathode, rbg) [package="5 mm [THT]"]
  LED8 = RGB LED (com. cathode, rbg) [package="5 mm [THT]"]
  LED9 = RGB LED (com. cathode, rbg) [package="5 mm [THT]"]
  LED10 = RGB LED (com. cathode, rbg) [package="5 mm [THT]"]
  R1 = Resistor [tolerance=±5% resistance=220 package=THT]
  R2 = Resistor [tolerance=±5% resistance=220 package=THT]
  R3 = Resistor [tolerance=±5% resistance=220 package=THT]
  R4 = Resistor [tolerance=±5% resistance=220 package=THT]
  R5 = Resistor [tolerance=±5% resistance=220 package=THT]
  R6 = Resistor [tolerance=±5% resistance=220 package=THT]
  R7 = Resistor [tolerance=±5% resistance=220 package=THT]
  R8 = Resistor [tolerance=±5% resistance=220 package=THT]
  R9 = Resistor [tolerance=±5% resistance=220 package=THT]
  R10 = Resistor [tolerance=±5% resistance=220 package=THT]
  R11 = Resistor [tolerance=±5% resistance=220 package=THT]
  R12 = Resistor [tolerance=±5% resistance=220 package=THT]
  R13 = Resistor [tolerance=±5% resistance=220 package=THT]
  R14 = Resistor [tolerance=±5% resistance=220 package=THT]
  R15 = Resistor [tolerance=±5% resistance=220 package=THT]
  R16 = Resistor [tolerance=±5% resistance=220 package=THT]
  R17 = Resistor [tolerance=±5% resistance=220 package=THT]
  R18 = Resistor [tolerance=±5% resistance=220 package=THT]
  R19 = Resistor [tolerance=±5% resistance=220 package=THT]
  R20 = Resistor [tolerance=±5% resistance=220 package=THT]
  R21 = Resistor [tolerance=±5% resistance=220 package=THT]
  R22 = Resistor [tolerance=±5% resistance=220 package=THT]
  R23 = Resistor [tolerance=±5% resistance=220 package=THT]
  R24 = Resistor [tolerance=±5% resistance=220 package=THT]
  R25 = Resistor [tolerance=±5% resistance=220 package=THT]
  R26 = Resistor [tolerance=±5% resistance=220 package=THT]
  R27 = Resistor [tolerance=±5% resistance=220 package=THT]
  R28 = Resistor [tolerance=±5% resistance=220 package=THT]
  R29 = Resistor [tolerance=±5% resistance=220 package=THT]
  R30 = Resistor [tolerance=±5% resistance=220 package=THT]
  U1 = 74HC595 [package="DIP16 [THT]"]
  U2 = 74HC595 [package="DIP16 [THT]"]
  U3 = 74HC595 [package="DIP16 [THT]"]
  U4 = 74HC595 [package="DIP16 [THT]"]
  IC1 = Hex Inverter Schmitt Trigger SN74HC14 [package="DIP (Dual Inline)"]
  S1 = Pushbutton [package="[THT]"]
  R31 = Resistor [tolerance=±5% resistance=10k package=THT]
  C1 = Electrolytic Capacitor [capacitance=0.22mF voltage=35V package="100 mil [THT, electrolytic]"]
  R32 = Rotary Potentiometer (Small) [maximum_resistance=10kΩ package=THT]
  Arduino1 = Arduino Uno (Rev3)

nets:
  N1: LED1.red_anode, R2.Pin_0
  GND: LED1.common_cathode, LED2.common_cathode, LED3.common_cathode, LED4.common_cathode, LED5.common_cathode, LED6.common_cathode, LED8.common_cathode, LED9.common_cathode, LED10.common_cathode, U1.GND, U1.OE, U2.GND, U2.OE, U3.GND, U3.OE, U4.GND, U4.OE, IC1.GND, S1.Pin_1, S1.Pin_2, C1.-, R32.leg2
  N2: LED1.blue_anode, R3.Pin_0
  N3: LED1.green_anode, R1.Pin_0
  N4: LED2.red_anode, R5.Pin_0
  N5: LED2.blue_anode, R6.Pin_0
  N6: LED2.green_anode, R4.Pin_0
  N7: LED3.red_anode, R8.Pin_0
  N8: LED3.blue_anode, R9.Pin_0
  N9: LED3.green_anode, R7.Pin_0
  N10: LED4.red_anode, R11.Pin_0
  N11: LED4.blue_anode, R12.Pin_0
  N12: LED4.green_anode, R10.Pin_0
  N13: LED5.red_anode, R14.Pin_0
  N14: LED5.blue_anode, R15.Pin_0
  N15: LED5.green_anode, R13.Pin_0
  N16: LED6.red_anode, R17.Pin_0
  N17: LED6.blue_anode, R18.Pin_0
  N18: LED6.green_anode, R16.Pin_0
  N19: LED7.red_anode, R20.Pin_0
  N20: LED7.blue_anode, R21.Pin_0
  N21: LED7.green_anode, R19.Pin_0
  N22: LED8.red_anode, R23.Pin_0
  N23: LED8.blue_anode, R24.Pin_0
  N24: LED8.green_anode, R22.Pin_0
  N25: LED9.red_anode, R26.Pin_0
  N26: LED9.blue_anode, R27.Pin_0
  N27: LED9.green_anode, R25.Pin_0
  N28: LED10.red_anode, R29.Pin_0
  N29: LED10.blue_anode, R30.Pin_0
  N30: LED10.green_anode, R28.Pin_0
  N31: R1.Pin_1, U1.Q1
  N32: R2.Pin_1, U1.Q0
  N33: R3.Pin_1, U1.Q2
  N34: R4.Pin_1, U1.Q4
  N35: R5.Pin_1, U1.Q3
  N36: R6.Pin_1, U1.Q5
  N37: R7.Pin_1, U1.Q7
  N38: R8.Pin_1, U1.Q6
  N39: R9.Pin_1, U2.Q0
  N40: R10.Pin_1, U2.Q2
  N41: R11.Pin_1, U2.Q1
  N42: R12.Pin_1, U2.Q3
  N43: R13.Pin_1, U2.Q5
  N44: R14.Pin_1, U2.Q4
  N45: R15.Pin_1, U2.Q6
  N46: R16.Pin_1, U3.Q0
  N47: R17.Pin_1, U2.Q7
  N48: R18.Pin_1, U3.Q1
  N49: R19.Pin_1, U3.Q3
  N50: R20.Pin_1, U3.Q2
  N51: R21.Pin_1, U3.Q4
  N52: R22.Pin_1, U3.Q6
  N53: R23.Pin_1, U3.Q5
  N54: R24.Pin_1, U3.Q7
  N55: R25.Pin_1, U4.Q1
  N56: R26.Pin_1, U4.Q0
  N57: R27.Pin_1, U4.Q2
  N58: R28.Pin_1, U4.Q4
  N59: R29.Pin_1, U4.Q3
  N60: R30.Pin_1, U4.Q5
  N61: U1.Q7', U2.DS
  VCC: U1.MR, U1.VCC, U2.MR, U2.VCC, U3.MR, U3.VCC, U4.MR, U4.VCC, IC1.VCC, R31.Pin_0, R32.leg1
  N62: U1.SH_CP, U2.SH_CP, U3.SH_CP, U4.SH_CP
  N63: U1.ST_CP, U2.ST_CP, U3.ST_CP, U4.ST_CP
  N64: U1.DS, Arduino1.D8
  N65: U2.Q7', U3.DS
  N66: U3.Q7', U4.DS
  N67: IC1.1A, S1.Pin_3, S1.Pin_4, R31.Pin_1, C1.+
  N68: IC1.1Y, Arduino1.D2
  N69: R32.wiper, Arduino1.A0
